# Fritzing sketch ECG (saved by Fritzing 0.9.3b)
breadboards: 1

parts:
  EXG1 = BioAmp ECG Pill
  Part1 = Arduino Nano (Rev3.0)

nets:
  N1: EXG1.1, EXG1.3
  N2: EXG1.4, Part1.VIN
  N3: EXG1.5, Part1.RESET
  N4: EXG1.6, Part1.A1

notes:
  Reference Probe
  IN+ Probe
  IN- Probe

custom parts:
  BioAmp ECG Pill: BioAmp EXG Pill is a small, powerful Analog Front End (AFE) biopotential signal acquisition board that can be paired with any 5 V Micro Controller Unit (MCU) with an ADC. It is capable of recording publication-quality biopotential signals like ECG, EMG, EOG, and EEG, without the inclusion of any dedicated hardware or software filters. It’s small size allows easy integration into mobile and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
