# Fritzing sketch Sp02_BPM_Alert_Design (saved by Fritzing 0.9.3b)

parts:
  Raspberry_Pi_1 = Raspberry Pi 4 [part_number=RPI-4-b]
  M1 = MAX30102
  Part1 = InvenSense MPU6050  # not connected
  A1 = Sim900a module

nets:
  3V3: Raspberry_Pi_1.3v3, M1.VIN
  N1: Raspberry_Pi_1.GPIO2, M1.SDA
  N2: Raspberry_Pi_1.GPIO3, M1.SCL
  N3: Raspberry_Pi_1.GPIO15, A1.Pin_14
  N4: Raspberry_Pi_1.GPIO14, A1.Pin_11
  GND: Raspberry_Pi_1.GND, M1.GND
  N5: Raspberry_Pi_1.5V, A1.Pin_15

notes:
  Raspberry Pi 4B
  SIM900A
  MPU6050
  MAX30100

custom parts:
  Raspberry Pi 4: The RPi4, a faster version of the awesome Raspberry Pi 2 B ARM Board with 40 pin gpio. Ready for special Raspberry Pi B+ and RPi2 Hat (Hardware attached (on) top)
  MAX30102: Oximeter module using the MAX30102 chip. You may wish to read (and check your module) this post on power problems with these modules: https://reedpaper.wordpress.com/2018/08/22/pulse-oximeter-max30100-max30102-how-to-fix-wrong-board/ . As usual, if you want the mounting holes in pcb, you need to drag a hole over the pad in silkscreen to actually drill the hole (by default they are not drilled)
  Sim900a module: SIM900A GSM module delivers GSM/GPRS 900/1800MHz performance for voice, SMS, Data, and Fax in a small form factor and with low power consumption.
